# Fritzing sketch Fritzing (saved by Fritzing 0.9.2b)
breadboards: 1

parts:
  J1 = Basic Servo
  J2 = Basic Servo
  Netduino1 = Netduino

nets:
  GND: J1.gnd, J2.gnd, Netduino1.GND
  VCC: J1.vcc, J2.vcc, Netduino1.+5V
  N1: J1.pulse, Netduino1.D6_PWM1
  N2: J2.pulse, Netduino1.D8_CTS1
